// Logisim project PROCESSADOR_BIPFINISHED.circ as structural Verilog: 12 circuits, main circuit main
module main (
);

  wire caminho_controle_1_en_ram, caminho_controle_1_en_rom, caminho_controle_1_sel_op2,
       caminho_controle_1_sel_ula, caminho_controle_1_wr_acc, caminho_controle_1_wr_ram, caminho_dados_1_op0,
       caminho_dados_1_op1, caminho_dados_1_op2, caminho_dados_1_op3, CLOCK_out, RESET_out;
  wire [1:0] caminho_controle_1_sel_op1;
  wire [11:0] caminho_controle_1_add_rom, caminho_dados_1_add_ram;
  wire [15:0] caminho_dados_1_din_ram, ram_1_data, rom_1_data;

  Button RESET (.out(RESET_out));
  Clock CLOCK (.out(CLOCK_out));
  RAM #(.addrWidth(12), .dataWidth(16), .bus("separate")) ram_1 (
    .addr(caminho_dados_1_add_ram), .din(caminho_dados_1_din_ram), .data(ram_1_data),
    .str(caminho_controle_1_wr_ram), .sel(caminho_controle_1_en_ram), .clk(CLOCK_out), .ld(1'b1),
    .clr(RESET_out));
  ROM #(.addrWidth(12), .dataWidth(16)) rom_1 (.addr(caminho_controle_1_add_rom), .data(rom_1_data), .sel(1'b1));
  CAMINHO_DADOS caminho_dados_1 (
    .SEL_OP1(caminho_controle_1_sel_op1), .DOUT_RAM(ram_1_data), .SEL_OP2(caminho_controle_1_sel_op2),
    .CLOCK(CLOCK_out), .DOUT_ROM(rom_1_data), .ADD_RAM(caminho_dados_1_add_ram),
    .WR_ACC(caminho_controle_1_wr_acc), .DIN_RAM(caminho_dados_1_din_ram),
    .SEL_ULA(caminho_controle_1_sel_ula), .OP0(caminho_dados_1_op0), .OP1(caminho_dados_1_op1),
    .OP2(caminho_dados_1_op2), .OP3(caminho_dados_1_op3));  // open: resposta
  CAMINHO_CONTROLE caminho_controle_1 (
    .CLOCK(CLOCK_out), .OP3(caminho_dados_1_op3), .OP2(caminho_dados_1_op2), .OP1(caminho_dados_1_op1),
    .OP0(caminho_dados_1_op0), .ADD_ROM(caminho_controle_1_add_rom), .EN_ROM(caminho_controle_1_en_rom),
    .EN_RAM(caminho_controle_1_en_ram), .WR_RAM(caminho_controle_1_wr_ram),
    .WR_ACC(caminho_controle_1_wr_acc), .SEL_OP1(caminho_controle_1_sel_op1),
    .SEL_OP2(caminho_controle_1_sel_op2), .SEL_ULA(caminho_controle_1_sel_ula));

  // Notes on the sheet:
  //   contents of rom_1 (hex, n*v repeats v):
  //   3015 1000 300a 1001 300d 1002 3040 1003 307a 1004 300a 7005 4004 6001 7011 1005 5016 6004 1006
endmodule

module ULA (
  input  [15:0] A,
  input  [15:0] B,
  input  SEL_ULA,
  output [15:0] S
);

  wire [15:0] adder_1_out, subtractor_1_out;

  Adder #(.width(16)) adder_1 (.a(A), .b(B), .out(adder_1_out));  // open: cin, cout
  Subtractor #(.width(16)) subtractor_1 (.a(A), .b(B), .out(subtractor_1_out));  // open: bin, bout
  Multiplexer #(.width(16), .enable("false")) multiplexer_1 (
    .in0(adder_1_out), .in1(subtractor_1_out), .out(S), .sel(SEL_ULA));
endmodule

// DADOS
module CAMINHO_DADOS (
  input  CLOCK,
  input  [1:0] SEL_OP1,
  input  WR_ACC,
  input  [15:0] DOUT_RAM,
  input  [15:0] DOUT_ROM,
  input  SEL_ULA,
  input  SEL_OP2,
  output [15:0] resposta,
  output [11:0] ADD_RAM,
  output [15:0] DIN_RAM,
  output OP0,
  output OP1,
  output OP2,
  output OP3
);

  wire [15:0] multiplexer_1_out, multiplexer_2_out;

  Register #(.width(16)) IR (.D(DOUT_ROM), .Q({OP3, OP2, OP1, OP0, ADD_RAM}), .clk(CLOCK));  // open: en, clr
  Register #(.width(16)) ACC (.D(multiplexer_1_out), .en(WR_ACC), .Q(DIN_RAM), .clk(CLOCK));  // open: clr
  Multiplexer #(.select(2), .width(16), .enable("false")) multiplexer_1 (
    .in0(resposta), .in1({4'b0000, ADD_RAM}), .in2(DOUT_RAM), .out(multiplexer_1_out), .sel(SEL_OP1));  // open: in3
  Multiplexer #(.width(16), .enable("false")) multiplexer_2 (
    .in0({4'b0000, ADD_RAM}), .in1(DOUT_RAM), .out(multiplexer_2_out), .sel(SEL_OP2));
  ULA ula_1 (.A(DIN_RAM), .B(multiplexer_2_out), .SEL_ULA(SEL_ULA), .S(resposta));
endmodule

// CONTROLE
module CAMINHO_CONTROLE (
  input  CLOCK,
  input  OP3,
  input  OP2,
  input  OP1,
  input  OP0,
  output [11:0] ADD_ROM,
  output EN_ROM,
  output EN_RAM,
  output WR_RAM,
  output WR_ACC,
  output [1:0] SEL_OP1,
  output SEL_OP2,
  output SEL_ULA
);

  wire logica_controle_1_en_pc;

  LOGICA_CONTROLE logica_controle_1 (
    .OP3(OP3), .OP2(OP2), .OP1(OP1), .OP0(OP0), .EN_PC(logica_controle_1_en_pc), .EN_ROM(EN_ROM),
    .EN_RAM(EN_RAM), .WR_RAM(WR_RAM), .WR_ACC(WR_ACC), .SEL_OP1(SEL_OP1), .SEL_OP2(SEL_OP2), .SEL_ULA(SEL_ULA));
  PROGRAMM_COUNTER programm_counter_1 (.CLOCK(CLOCK), .EN_PC(logica_controle_1_en_pc), .ADD_ROM(ADD_ROM));
endmodule

// PC
module PROGRAMM_COUNTER (
  input  CLOCK,
  input  EN_PC,
  output [11:0] ADD_ROM
);

  wire [11:0] adder_1_out;

  Adder #(.width(12)) adder_1 (.a(ADD_ROM), .b(12'h1), .out(adder_1_out));  // open: cin, cout
  Register #(.width(12)) PC (.D(adder_1_out), .en(EN_PC), .Q(ADD_ROM), .clk(CLOCK));  // open: clr
endmodule

// LOG_CONTROL
module LOGICA_CONTROLE (
  input  OP3,
  input  OP2,
  input  OP1,
  input  OP0,
  output EN_PC,
  output EN_ROM,
  output EN_RAM,
  output WR_RAM,
  output WR_ACC,
  output [1:0] SEL_OP1,
  output SEL_OP2,
  output SEL_ULA
);

  WR_RAM wr_ram_1 (.OP3(OP3), .OP2(OP2), .OP1(OP1), .OP0(OP0), .out_5(WR_RAM));
  or or_1 (EN_PC, OP0, OP1, OP2, OP3);
  or or_2 (EN_ROM, OP0, OP1, OP2, OP3);
  EN_RAM en_ram_1 (.OP3(OP3), .OP2(OP2), .OP1(OP1), .OP0(OP0), .EN_RAM(EN_RAM));
  WR_ACC wr_acc_1 (.OP3(OP3), .OP2(OP2), .OP1(OP1), .OP0(OP0), .out_5(WR_ACC));
  SEL_OP1 sel_op1_1 (.OP3(OP3), .OP2(OP2), .OP1(OP1), .OP0(OP0), .SEL_OP1(SEL_OP1));
  SEL_OP2 sel_op2_1 (.OP3(OP3), .OP2(OP2), .OP1(OP1), .OP0(OP0), .SEL_OP2(SEL_OP2));
  SEL_ULA sel_ula_1 (.OP3(OP3), .OP2(OP2), .OP1(OP1), .OP0(OP0), .out_5(SEL_ULA));
endmodule

module EN_RAM (
  input  OP3,
  input  OP2,
  input  OP1,
  input  OP0,
  output EN_RAM
);

  wire and_1_out, and_2_out, and_3_out, and_4_out, not_1_out, not_2_out, not_3_out, not_4_out, not_5_out,
       not_6_out, not_7_out, not_8_out, not_9_out, not_10_out, not_11_out;

  not not_1 (not_1_out, OP1);
  not not_2 (not_2_out, OP2);
  not not_3 (not_3_out, OP3);
  not not_4 (not_4_out, OP0);
  not not_5 (not_5_out, OP2);
  not not_6 (not_6_out, OP3);
  not not_7 (not_7_out, OP0);
  not not_8 (not_8_out, OP1);
  not not_9 (not_9_out, OP3);
  not not_10 (not_10_out, OP0);
  not not_11 (not_11_out, OP3);
  and and_1 (and_1_out, OP0, not_1_out, not_2_out, not_3_out);
  and and_2 (and_2_out, not_4_out, OP1, not_5_out, not_6_out);
  and and_3 (and_3_out, not_7_out, not_8_out, OP2, not_9_out);
  and and_4 (and_4_out, not_10_out, OP1, OP2, not_11_out);
  or or_1 (EN_RAM, and_1_out, and_2_out, and_3_out, and_4_out);
endmodule

module SEL_OP2 (
  input  OP3,
  input  OP2,
  input  OP1,
  input  OP0,
  output SEL_OP2
);

  wire and_1_out, and_2_out, not_1_out, not_2_out, not_3_out, not_4_out, not_5_out;

  not not_1 (not_1_out, OP0);
  not not_2 (not_2_out, OP1);
  not not_3 (not_3_out, OP3);
  not not_4 (not_4_out, OP0);
  not not_5 (not_5_out, OP3);
  and and_1 (and_1_out, not_1_out, not_2_out, OP2, not_3_out);
  and and_2 (and_2_out, not_4_out, OP1, OP2, not_5_out);
  or or_1 (SEL_OP2, and_1_out, and_2_out);
endmodule

module SEL_OP1 (
  input  OP3,
  input  OP2,
  input  OP1,
  input  OP0,
  output [1:0] SEL_OP1
);

  wire not_1_out, not_2_out, not_3_out, not_4_out, not_5_out;

  not not_1 (not_1_out, OP2);
  not not_2 (not_2_out, OP3);
  not not_3 (not_3_out, OP0);
  not not_4 (not_4_out, OP2);
  not not_5 (not_5_out, OP3);
  and BIT0 (SEL_OP1[0], OP0, OP1, not_1_out, not_2_out);
  and BIT1 (SEL_OP1[1], not_3_out, OP1, not_4_out, not_5_out);
endmodule

module WR_RAM (
  input  OP3,
  input  OP2,
  input  OP1,
  input  OP0,
  output out_5
);

  wire not_1_out, not_2_out, not_3_out;

  not not_1 (not_1_out, OP1);
  not not_2 (not_2_out, OP2);
  not not_3 (not_3_out, OP3);
  and and_1 (out_5, OP0, not_1_out, not_2_out, not_3_out);
endmodule

module WR_ACC (
  input  OP3,
  input  OP2,
  input  OP1,
  input  OP0,
  output out_5
);

  wire not_1_out, or_1_out, or_2_out;

  not not_1 (not_1_out, OP0);
  or or_1 (or_1_out, OP0, OP1, OP2, OP3);
  or or_2 (or_2_out, not_1_out, OP1, OP2, OP3);
  and and_1 (out_5, or_1_out, or_2_out);
endmodule

module SEL_ULA (
  input  OP3,
  input  OP2,
  input  OP1,
  input  OP0,
  output out_5
);

  wire and_1_out, and_2_out, not_1_out, not_2_out, not_3_out;

  not not_1 (not_1_out, OP0);
  not not_2 (not_2_out, OP3);
  not not_3 (not_3_out, OP3);
  and and_1 (and_1_out, not_1_out, OP1, OP2, not_2_out);
  and and_2 (and_2_out, OP0, OP1, OP2, not_3_out);
  or or_1 (out_5, and_1_out, and_2_out);
endmodule
